# Fritzing sketch l293d (saved by Fritzing 0.9.3b)
breadboards: 1

parts:
  IC1 = L293D [package=THT]
  M1 = DC Motor
  M2 = DC Motor
  IC2 = Voltage Regulator [package=to220-igo]
  BAT1 = BC9VPC [package=bc9vpc]
  Part1 = Arduino Uno (Rev3)

nets:
  N1: IC1.Enable_1, IC1.Enable_2, IC1.+V, IC2.OUT, Part1.VIN
  N2: IC1.In_1, Part1.D5_PWM
  N3: IC1.Out_1_(_Controlled_by_Enable_1_), M2.pin_2
  GND: IC1.0V, IC2.GND, BAT1.V-, Part1.GND
  N4: IC1.Out_2_(_Controlled_by_Enable_1_), M2.pin_1
  N5: IC1.In_2, Part1.D4
  N6: IC1.+Vmotor, IC2.IN, BAT1.V+
  N7: IC1.In_3, Part1.D3_PWM
  N8: IC1.Out_3_(_Controlled_by_Enable_2_), M1.pin_2
  N9: IC1.Out_4_(_Controlled_by_Enable_2_), M1.pin_1
  N10: IC1.In_4, Part1.D2
