# Fritzing sketch lcd (saved by Fritzing 0.9.3b)
breadboards: 1

parts:
  LCD1 = LCD screen
  R1 = Rotary Potentiometer (Small) [maximum_resistance=100kΩ package=THT]
  Part1 = Arduino Uno (Rev3)
  R2 = Resistor [tolerance=±5% resistance=220 package=THT]

nets:
  N1: LCD1.VSS, LCD1.R/W, LCD1.LED+, R1.leg1
  N2: LCD1.VDD, R1.leg2, R2.Pin_1
  N3: LCD1.V0, R1.wiper
  N4: LCD1.RS, Part1.D7
  N5: LCD1.E, Part1.D6_PWM
  N6: LCD1.DB4, Part1.D2
  N7: LCD1.DB5, Part1.D3_PWM
  N8: LCD1.DB6, Part1.D4
  N9: LCD1.DB7, Part1.D5_PWM
  N10: LCD1.LED-, R2.Pin_0
