# Fritzing sketch pump (saved by Fritzing 0.9.3b)
breadboards: 1

parts:
  Q1 = MOSFET-NCHANNEL [package=to220v]
  Part1 = Arduino Uno (Rev3)
  M1 = DC Motor
  R1 = Resistor [tolerance=±5% resistance=10k package=THT]
  VCC1 = Battery block 9V

nets:
  N1: Q1.G, Part1.GND, R1.Pin_1, VCC1.-
  N2: Q1.D, Part1.D9_PWM, R1.Pin_0
  N3: Q1.S, M1.pin_2
  N4: Part1.5V, M1.pin_1, VCC1.+
