# Fritzing sketch wifi (saved by Fritzing 0.9.3b)
breadboards: 1

parts:
  U1 = NodeMCU V3.0
  Part1 = Arduino Uno (Rev3)
  LED1 = LED - 5mm [color="Red (633nm)" package="5 mm [THT]"]
  R1 = Resistor [tolerance=±5% resistance=220 package=THT]

nets:
  N1: U1.RX, Part1.D1/TX
  N2: U1.TX, Part1.D0/RX
  N3: Part1.D8, LED1.anode
  N4: Part1.GND, R1.Pin_0
  N5: LED1.cathode, R1.Pin_1

custom parts:
  NodeMCU V3.0: ESP8266 based NodeMCU
